# Fritzing sketch design (saved by Fritzing 0.9.3b)
breadboards: 1

parts:
  Relay = Keyes Relay [package=THT]
  LED2 = smd LED [color="Red (633nm)" package="0805 [SMD]"]
  R1 = Resistor [tolerance=±5% resistance=10k package=THT]
  Part2 = Arduino Uno (Rev3) - ICSP

nets:
  N1: Relay.signal, Relay.C, Part2.5V
  N2: Relay.power, LED2.cathode, Part2.GND
  N3: Relay.ground, Part2.D2
  N4: Relay.NO, R1.Pin_0
  N5: LED2.anode, R1.Pin_1

custom parts:
  Keyes Relay: The Keyes 5V relay module is suitable for SCM development, home appliance control. It uses a 5V~12V TIL control signal which can control DC / AC signal.
